// Logisim project proyecto reloj.circ as structural Verilog: 3 circuits, main circuit contador 
module contador (
  input  in_1,
  input  in_2,
  input  in_3,
  input  in_4,
  input  in_5,
  output out_6,
  output out_7,
  output out_8,
  output out_9
);

  wire and_1_out, and_2_out, and_3_out, and_4_out, j_k_ff_2_qn, j_k_ff_4_qn, or_1_out, or_2_out;

  or or_1 (or_1_out, j_k_ff_4_qn, j_k_ff_2_qn);
  J_K_Flip_Flop j_k_ff_1 (
    .J(or_1_out), .clk(in_1), .K(in_1), .Q(out_9), .preset(and_1_out), .en(1'b1), .reset(and_4_out));  // open: Qn
  and and_1 (and_1_out, in_4, in_5);
  or or_2 (or_2_out, out_6, out_9);
  J_K_Flip_Flop j_k_ff_2 (
    .J(out_9), .clk(in_1), .K(or_2_out), .Q(out_8), .Qn(j_k_ff_2_qn), .preset(and_1_out), .reset(and_4_out));  // open: en
  and and_2 (and_2_out, out_9, out_8);
  J_K_Flip_Flop j_k_ff_3 (
    .J(and_2_out), .clk(in_1), .K(and_2_out), .Q(out_7), .preset(and_4_out), .reset(and_4_out));  // open: Qn, en
  and and_3 (and_3_out, out_9, out_7, out_8);
  and and_4 (and_4_out, in_2, in_3);
  J_K_Flip_Flop j_k_ff_4 (
    .J(and_3_out), .clk(in_1), .K(out_8), .Q(out_6), .Qn(j_k_ff_4_qn), .preset(and_1_out), .reset(and_4_out));  // open: en
endmodule

module h (
  input  s4,
  input  s3,
  input  s2,
  input  s1,
  output out_5,
  output out_6,
  output out_7,
  output out_8,
  output out_9,
  output out_10,
  output out_11
);

  wire and_1_out, and_2_out, and_3_out, and_4_out, and_5_out, and_6_out, and_7_out, and_8_out, and_9_out,
       and_10_out, and_11_out, and_12_out, and_13_out, and_14_out, and_15_out, and_16_out, and_17_out,
       not_1_out, not_2_out, not_3_out, not_4_out, not_5_out, not_6_out, not_7_out, not_8_out, not_9_out,
       not_10_out, not_11_out, not_12_out, not_13_out, not_14_out, not_15_out, not_16_out, not_17_out,
       not_18_out, not_19_out, not_20_out, not_21_out, or_1_out, or_2_out, or_4_out, or_5_out, or_7_out,
       or_9_out, or_10_out, or_13_out, or_15_out, or_16_out, or_18_out;

  not not_1 (not_1_out, s3);
  not not_2 (not_2_out, s1);
  and and_1 (and_1_out, not_1_out, not_2_out);
  or or_1 (or_1_out, and_1_out, s2);
  and and_2 (and_2_out, s3, s1);
  or or_2 (or_2_out, and_2_out, s4);
  or or_3 (out_5, or_1_out, or_2_out);
  not not_3 (not_3_out, s3);
  not not_4 (not_4_out, s2);
  or or_4 (or_4_out, not_3_out, and_3_out);
  not not_5 (not_5_out, s1);
  and and_3 (and_3_out, not_4_out, not_5_out);
  and and_4 (and_4_out, s2, s1);
  or or_5 (or_5_out, and_4_out, s4);
  or or_6 (out_6, or_4_out, or_5_out);
  not not_6 (not_6_out, s2);
  or or_7 (or_7_out, not_6_out, s1);
  or or_8 (out_7, or_7_out, s3);
  not not_7 (not_7_out, s3);
  not not_8 (not_8_out, s1);
  not not_9 (not_9_out, s3);
  and and_5 (and_5_out, not_9_out, not_8_out);
  and and_6 (and_6_out, not_7_out, s2);
  or or_9 (or_9_out, and_5_out, and_6_out);
  not not_10 (not_10_out, s1);
  and and_7 (and_7_out, s2, not_10_out);
  or or_10 (or_10_out, and_7_out, and_10_out);
  or or_11 (out_8, or_9_out, or_10_out);
  not not_11 (not_11_out, s2);
  not not_12 (not_12_out, s3);
  and and_8 (and_8_out, s3, not_11_out);
  and and_9 (and_9_out, not_12_out, not_14_out);
  and and_10 (and_10_out, and_8_out, s1);
  not not_13 (not_13_out, s1);
  not not_14 (not_14_out, s1);
  not not_15 (not_15_out, s2);
  and and_11 (and_11_out, s2, not_13_out);
  or or_12 (out_9, and_9_out, and_11_out);
  not not_16 (not_16_out, s2);
  not not_17 (not_17_out, s1);
  and and_12 (and_12_out, s3, not_16_out);
  and and_13 (and_13_out, not_15_out, not_17_out);
  or or_13 (or_13_out, and_13_out, and_12_out);
  or or_14 (out_10, or_13_out, or_15_out);
  not not_18 (not_18_out, s1);
  and and_14 (and_14_out, s3, not_18_out);
  or or_15 (or_15_out, and_14_out, s4);
  not not_19 (not_19_out, s3);
  and and_15 (and_15_out, not_19_out, s2);
  and and_16 (and_16_out, s2, not_20_out);
  or or_16 (or_16_out, and_15_out, and_16_out);
  not not_20 (not_20_out, s1);
  not not_21 (not_21_out, s2);
  and and_17 (and_17_out, s3, not_21_out);
  or or_17 (out_11, or_16_out, or_18_out);
  or or_18 (or_18_out, and_17_out, s4);
endmodule

module main (
);

  wire and_1_out, and_2_out, and_3_out, and_4_out, and_5_out, and_6_out, clock_1_out, contador_1_out_6,
       contador_1_out_7, contador_1_out_8, contador_1_out_9, contador_2_out_6, contador_2_out_7,
       contador_2_out_8, contador_2_out_9, contador_3_out_6, contador_3_out_7, contador_3_out_8,
       contador_3_out_9, contador_4_out_6, contador_4_out_7, contador_4_out_8, contador_4_out_9,
       contador_5_out_6, contador_5_out_7, contador_5_out_8, contador_5_out_9, contador_6_out_6,
       contador_6_out_7, contador_6_out_8, contador_6_out_9, h_1_out_5, h_1_out_6, h_1_out_7, h_1_out_8,
       h_1_out_9, h_1_out_10, h_1_out_11, h_2_out_5, h_2_out_6, h_2_out_7, h_2_out_8, h_2_out_9, h_2_out_10,
       h_2_out_11, h_3_out_5, h_3_out_6, h_3_out_7, h_3_out_8, h_3_out_9, h_3_out_10, h_3_out_11, h_4_out_5,
       h_4_out_6, h_4_out_7, h_4_out_8, h_4_out_9, h_4_out_10, h_4_out_11, h_5_out_5, h_5_out_6, h_5_out_7,
       h_5_out_8, h_5_out_9, h_5_out_10, h_5_out_11, h_6_out_5, h_6_out_6, h_6_out_7, h_6_out_8, h_6_out_9,
       h_6_out_10, h_6_out_11, xor_1_out;

  h h_1 (
    .s4(contador_1_out_6), .s3(contador_1_out_7), .s2(contador_1_out_8), .s1(contador_1_out_9),
    .out_5(h_1_out_5), .out_6(h_1_out_6), .out_7(h_1_out_7), .out_8(h_1_out_8), .out_9(h_1_out_9),
    .out_10(h_1_out_10), .out_11(h_1_out_11));
  contador contador_1 (
    .in_1(and_1_out), .in_4(1'b0), .in_5(1'b0), .in_2(and_2_out), .in_3(1'b1), .out_6(contador_1_out_6),
    .out_7(contador_1_out_7), .out_8(contador_1_out_8), .out_9(contador_1_out_9));
  _7_Segment_Display u_7_segment_display_1 (
    .g(h_1_out_5), .f(h_1_out_6), .a(h_1_out_11), .b(h_1_out_10), .e(h_1_out_7), .d(h_1_out_8), .c(h_1_out_9));  // open: dp
  and and_1 (and_1_out, contador_2_out_6, contador_2_out_8);
  xor xor_1 (xor_1_out, and_1_out, and_2_out);
  h h_2 (
    .s4(contador_2_out_6), .s3(contador_2_out_7), .s2(contador_2_out_8), .s1(contador_2_out_9),
    .out_5(h_2_out_5), .out_6(h_2_out_6), .out_7(h_2_out_7), .out_8(h_2_out_8), .out_9(h_2_out_9),
    .out_10(h_2_out_10), .out_11(h_2_out_11));
  contador contador_2 (
    .in_1(and_3_out), .in_4(1'b0), .in_5(1'b0), .in_2(xor_1_out), .in_3(1'b1), .out_6(contador_2_out_6),
    .out_7(contador_2_out_7), .out_8(contador_2_out_8), .out_9(contador_2_out_9));
  and and_2 (and_2_out, contador_1_out_8, contador_2_out_7);
  _7_Segment_Display u_7_segment_display_2 (
    .g(h_2_out_5), .f(h_2_out_6), .a(h_2_out_11), .b(h_2_out_10), .e(h_2_out_7), .d(h_2_out_8), .c(h_2_out_9));  // open: dp
  and and_3 (and_3_out, contador_3_out_7, contador_3_out_8);
  LED led_1 (.in(1'b1));
  LED led_2 (.in(1'b1));
  h h_3 (
    .s4(contador_3_out_6), .s3(contador_3_out_7), .s2(contador_3_out_8), .s1(contador_3_out_9),
    .out_5(h_3_out_5), .out_6(h_3_out_6), .out_7(h_3_out_7), .out_8(h_3_out_8), .out_9(h_3_out_9),
    .out_10(h_3_out_10), .out_11(h_3_out_11));
  contador contador_3 (
    .in_1(and_4_out), .in_4(1'b0), .in_5(1'b0), .in_2(and_3_out), .in_3(1'b1), .out_6(contador_3_out_6),
    .out_7(contador_3_out_7), .out_8(contador_3_out_8), .out_9(contador_3_out_9));
  _7_Segment_Display u_7_segment_display_3 (
    .g(h_3_out_5), .f(h_3_out_6), .a(h_3_out_11), .b(h_3_out_10), .e(h_3_out_8), .d(h_3_out_7), .c(h_3_out_9));  // open: dp
  and and_4 (and_4_out, contador_4_out_7, contador_4_out_8);
  h h_4 (
    .s4(contador_4_out_6), .s3(contador_4_out_7), .s2(contador_4_out_8), .s1(contador_4_out_9),
    .out_5(h_4_out_5), .out_6(h_4_out_6), .out_7(h_4_out_7), .out_8(h_4_out_8), .out_9(h_4_out_9),
    .out_10(h_4_out_10), .out_11(h_4_out_11));
  contador contador_4 (
    .in_1(and_5_out), .in_4(1'b0), .in_5(1'b0), .in_2(and_4_out), .in_3(1'b1), .out_6(contador_4_out_6),
    .out_7(contador_4_out_7), .out_8(contador_4_out_8), .out_9(contador_4_out_9));
  _7_Segment_Display u_7_segment_display_4 (
    .g(h_4_out_5), .f(h_4_out_6), .a(h_4_out_11), .b(h_4_out_10), .e(h_4_out_8), .d(h_4_out_7), .c(h_4_out_9));  // open: dp
  and and_5 (and_5_out, contador_5_out_7, contador_5_out_8);
  LED led_3 (.in(1'b1));
  LED led_4 (.in(1'b1));
  h h_5 (
    .s4(contador_5_out_6), .s3(contador_5_out_7), .s2(contador_5_out_8), .s1(contador_5_out_9),
    .out_5(h_5_out_5), .out_6(h_5_out_6), .out_7(h_5_out_7), .out_8(h_5_out_8), .out_9(h_5_out_9),
    .out_10(h_5_out_10), .out_11(h_5_out_11));
  contador contador_5 (
    .in_1(and_6_out), .in_4(1'b0), .in_5(1'b0), .in_2(and_5_out), .in_3(1'b1), .out_6(contador_5_out_6),
    .out_7(contador_5_out_7), .out_8(contador_5_out_8), .out_9(contador_5_out_9));
  _7_Segment_Display u_7_segment_display_5 (
    .g(h_5_out_5), .f(h_5_out_6), .a(h_5_out_11), .b(h_5_out_10), .e(h_5_out_8), .d(h_5_out_7), .c(h_5_out_9));  // open: dp
  h h_6 (
    .s4(contador_6_out_6), .s3(contador_6_out_7), .s2(contador_6_out_8), .s1(contador_6_out_9),
    .out_5(h_6_out_5), .out_6(h_6_out_6), .out_7(h_6_out_7), .out_8(h_6_out_8), .out_9(h_6_out_9),
    .out_10(h_6_out_10), .out_11(h_6_out_11));
  and and_6 (and_6_out, contador_6_out_8, contador_6_out_9);
  contador contador_6 (
    .in_1(clock_1_out), .in_4(1'b0), .in_5(1'b0), .in_2(and_6_out), .in_3(1'b1), .out_6(contador_6_out_6),
    .out_7(contador_6_out_7), .out_8(contador_6_out_8), .out_9(contador_6_out_9));
  Clock clock_1 (.out(clock_1_out));
  _7_Segment_Display u_7_segment_display_6 (
    .g(h_6_out_5), .f(h_6_out_6), .a(h_6_out_11), .b(h_6_out_10), .e(h_6_out_8), .d(h_6_out_7), .c(h_6_out_9));  // open: dp
endmodule
