// Logisim project tareaopcional2.circ as structural Verilog: 8 circuits, main circuit main
module main (
  input  in_1,
  input  in_2,
  input  in_3,
  input  in_4
);

  wire e1_1_out_5, e2_1_out_5, e3_1_out_5, e4_1_out_5, e5_1_out_5, e6_1_out_5, e7_1_out_5;

  E1 e1_1 (.a(in_1), .b(in_2), .c(in_3), .d(in_4), .out_5(e1_1_out_5));
  E2 e2_1 (.a(in_1), .b(in_2), .c(in_3), .d(in_4), .out_5(e2_1_out_5));
  E3 e3_1 (.in_1(in_1), .in_2(in_2), .in_3(in_3), .in_4(in_4), .out_5(e3_1_out_5));
  E4 e4_1 (.a(in_1), .b(in_2), .c(in_3), .d(in_4), .out_5(e4_1_out_5));
  E5 e5_1 (.a(in_1), .b(in_2), .c(in_3), .d(in_4), .out_5(e5_1_out_5));
  E6 e6_1 (.in_1(in_1), .in_2(in_2), .in_3(in_3), .in_4(in_4), .out_5(e6_1_out_5));
  E7 e7_1 (.in_1(in_1), .in_2(in_2), .in_3(in_3), .in_4(in_4), .out_5(e7_1_out_5));
  _7_Segment_Display u_7_segment_display_1 (
    .g(e1_1_out_5), .f(e2_1_out_5), .a(e3_1_out_5), .b(e4_1_out_5), .e(e5_1_out_5), .d(e6_1_out_5),
    .c(e7_1_out_5));  // open: dp
endmodule

module E1 (
  input  a,
  input  b,
  input  c,
  input  d,
  output out_5
);

  wire and_1_out, and_2_out, and_3_out, and_4_out, and_5_out, not_1_out, not_2_out, not_3_out, not_4_out,
       not_5_out, not_6_out;

  not not_1 (not_1_out, a);
  not not_2 (not_2_out, c);
  not not_3 (not_3_out, c);
  not not_4 (not_4_out, b);
  not not_5 (not_5_out, a);
  not not_6 (not_6_out, d);
  and and_1 (and_1_out, not_1_out, b, not_2_out);
  and and_2 (and_2_out, b, not_3_out, d);
  and and_3 (and_3_out, a, not_4_out);
  and and_4 (and_4_out, a, b, c);
  and and_5 (and_5_out, not_5_out, c, not_6_out);
  or or_1 (out_5, and_1_out, and_2_out, and_3_out, and_4_out, and_5_out);
endmodule

module E2 (
  input  a,
  input  b,
  input  c,
  input  d,
  output out_5
);

  wire and_1_out, and_2_out, and_3_out, and_4_out, and_5_out, and_6_out, not_1_out, not_2_out, not_3_out,
       not_4_out, not_5_out, not_6_out, not_7_out, not_8_out, not_9_out;

  not not_1 (not_1_out, a);
  not not_2 (not_2_out, b);
  not not_3 (not_3_out, d);
  not not_4 (not_4_out, a);
  not not_5 (not_5_out, c);
  not not_6 (not_6_out, c);
  not not_7 (not_7_out, d);
  not not_8 (not_8_out, b);
  not not_9 (not_9_out, d);
  and and_1 (and_1_out, not_1_out, not_2_out, not_3_out);
  and and_2 (and_2_out, not_4_out, b, not_5_out);
  and and_3 (and_3_out, a, not_6_out, not_7_out);
  and and_4 (and_4_out, a, not_8_out);
  and and_5 (and_5_out, a, b, c);
  and and_6 (and_6_out, b, c, not_9_out);
  or or_1 (out_5, and_1_out, and_2_out, and_3_out, and_4_out, and_5_out, and_6_out);
endmodule

module E3 (
  input  in_1,
  input  in_2,
  input  in_3,
  input  in_4,
  output out_5
);

  wire and_1_out, and_2_out, and_3_out, and_4_out, and_5_out, and_6_out, and_7_out, not_1_out, not_2_out,
       not_3_out, not_4_out, not_5_out, not_6_out, not_7_out, not_8_out, not_9_out, not_10_out;

  not not_1 (not_1_out, in_2);
  not not_2 (not_2_out, in_3);
  not not_3 (not_3_out, in_4);
  not not_4 (not_4_out, in_3);
  not not_5 (not_5_out, in_4);
  not not_6 (not_6_out, in_2);
  not not_7 (not_7_out, in_3);
  not not_8 (not_8_out, in_4);
  not not_9 (not_9_out, in_1);
  not not_10 (not_10_out, in_1);
  and and_1 (and_1_out, not_1_out, not_2_out, not_3_out);
  and and_2 (and_2_out, in_1, not_4_out, not_5_out);
  and and_3 (and_3_out, in_1, not_6_out, not_7_out);
  and and_4 (and_4_out, in_1, in_3, not_8_out);
  and and_5 (and_5_out, in_2, in_3, in_4);
  and and_6 (and_6_out, not_9_out, in_2, in_4);
  and and_7 (and_7_out, not_10_out, in_3);
  or or_1 (out_5, and_1_out, and_2_out, and_3_out, and_4_out, and_5_out, and_6_out, and_7_out);
endmodule

module E4 (
  input  a,
  input  b,
  input  c,
  input  d,
  output out_5
);

  wire and_1_out, and_2_out, and_3_out, and_4_out, and_5_out, not_1_out, not_2_out, not_3_out, not_4_out,
       not_5_out, not_6_out, not_7_out, not_8_out, not_9_out, not_10_out;

  not not_1 (not_1_out, b);
  not not_2 (not_2_out, c);
  not not_3 (not_3_out, b);
  not not_4 (not_4_out, d);
  not not_5 (not_5_out, a);
  not not_6 (not_6_out, a);
  not not_7 (not_7_out, c);
  not not_8 (not_8_out, d);
  not not_9 (not_9_out, a);
  not not_10 (not_10_out, b);
  and and_1 (and_1_out, a, not_1_out, not_2_out);
  and and_2 (and_2_out, not_3_out, c, not_4_out);
  and and_3 (and_3_out, not_5_out, c, d);
  and and_4 (and_4_out, not_6_out, not_7_out, not_8_out);
  and and_5 (and_5_out, not_9_out, not_10_out);
  or or_1 (out_5, and_1_out, and_2_out, and_3_out, and_4_out, and_5_out);
endmodule

module E5 (
  input  a,
  input  b,
  input  c,
  input  d,
  output out_5
);

  wire and_1_out, and_2_out, and_3_out, and_4_out, and_5_out, not_1_out, not_2_out, not_3_out, not_4_out,
       not_5_out, not_6_out, not_7_out, not_8_out;

  not not_1 (not_1_out, b);
  not not_2 (not_2_out, c);
  not not_3 (not_3_out, d);
  not not_4 (not_4_out, d);
  not not_5 (not_5_out, a);
  not not_6 (not_6_out, b);
  and and_1 (and_1_out, not_1_out, not_2_out, not_3_out);
  and and_2 (and_2_out, a, b, not_7_out);
  not not_7 (not_7_out, c);
  not not_8 (not_8_out, c);
  and and_3 (and_3_out, b, not_8_out, d);
  and and_4 (and_4_out, b, c, not_4_out);
  and and_5 (and_5_out, not_5_out, not_6_out, c);
  or or_1 (out_5, and_1_out, and_2_out, and_3_out, and_4_out, and_5_out);
endmodule

module E6 (
  input  in_1,
  input  in_2,
  input  in_3,
  input  in_4,
  output out_5
);

  wire and_1_out, and_2_out, and_3_out, and_4_out, and_5_out, and_6_out, not_1_out, not_2_out, not_3_out,
       not_4_out, not_5_out, not_6_out, not_7_out, not_8_out, not_9_out, not_10_out;

  not not_1 (not_1_out, in_2);
  not not_2 (not_2_out, in_3);
  not not_3 (not_3_out, in_4);
  not not_4 (not_4_out, in_3);
  not not_5 (not_5_out, in_4);
  not not_6 (not_6_out, in_3);
  not not_7 (not_7_out, in_2);
  not not_8 (not_8_out, in_1);
  not not_9 (not_9_out, in_4);
  not not_10 (not_10_out, in_4);
  and and_1 (and_1_out, not_1_out, not_2_out, not_3_out);
  and and_2 (and_2_out, in_1, not_4_out, not_5_out);
  and and_3 (and_3_out, in_2, not_6_out, in_4);
  and and_4 (and_4_out, not_7_out, in_3, in_4);
  and and_5 (and_5_out, not_8_out, not_9_out, in_3);
  and and_6 (and_6_out, in_2, in_3, not_10_out);
  or or_1 (out_5, and_1_out, and_3_out, and_4_out, and_5_out, and_2_out, and_6_out);
endmodule

module E7 (
  input  in_1,
  input  in_2,
  input  in_3,
  input  in_4,
  output out_5
);

  wire and_1_out, and_2_out, and_3_out, and_4_out, and_5_out, not_1_out, not_2_out, not_3_out, not_4_out,
       not_5_out, not_6_out, not_7_out, not_8_out, not_9_out;

  not not_1 (not_1_out, in_1);
  not not_2 (not_2_out, in_2);
  not not_3 (not_3_out, in_3);
  not not_4 (not_4_out, in_1);
  not not_5 (not_5_out, in_3);
  not not_6 (not_6_out, in_2);
  not not_7 (not_7_out, in_2);
  not not_8 (not_8_out, in_3);
  not not_9 (not_9_out, in_2);
  and and_1 (and_1_out, not_1_out, not_2_out, not_3_out);
  and and_2 (and_2_out, not_4_out, in_2);
  and and_3 (and_3_out, in_2, not_5_out, in_2);
  and and_4 (and_4_out, in_1, not_6_out, in_3);
  and and_5 (and_5_out, not_7_out, not_8_out, not_9_out);
  or or_1 (out_5, and_1_out, and_2_out, and_3_out, and_4_out, and_5_out);

  assign in_4 = in_2;
endmodule
